# Fritzing sketch pico8enc (saved by Fritzing 0.9.6b)
circuit board: 20.0182cm x 3.54716cm
breadboards: 1

parts:
  RE1 = Rotary Encoder [package=THT]
  RE2 = Rotary Encoder [package=THT]
  RE3 = Rotary Encoder [package=THT]
  RE4 = Rotary Encoder [package=THT]
  RE5 = Rotary Encoder [package=THT]
  RE6 = Rotary Encoder [package=THT]
  RE7 = Rotary Encoder [package=THT]
  RE8 = Rotary Encoder [package=THT]
  Pico = Raspberry Pi Pico

nets:
  N1: RE1.EncoderPinA, Pico.pin_17
  GND: RE1.EncoderPinC, RE1.SwitchrPinD, RE2.EncoderPinC, RE2.SwitchrPinD, RE3.EncoderPinC, RE3.SwitchrPinD, RE4.EncoderPinC, RE4.SwitchrPinD, RE5.EncoderPinC, RE5.SwitchrPinD, RE6.EncoderPinC, RE6.SwitchrPinD, RE7.EncoderPinC, RE7.SwitchrPinD, RE8.EncoderPinC, RE8.SwitchrPinD, Pico.pin_3, Pico.pin_23, Pico.pin_38, Pico.pin_42
  N2: RE1.EncoderPinB, Pico.pin_16
  re1sw: RE1.SwitchPinE, Pico.pin_21
  N3: RE2.EncoderPinA, Pico.pin_15
  N4: RE2.EncoderPinB, Pico.pin_14
  re2sw: RE2.SwitchPinE, Pico.pin_22
  N5: RE3.EncoderPinA, Pico.pin_12
  N6: RE3.EncoderPinB, Pico.pin_11
  re3sw: RE3.SwitchPinE, Pico.pin_24
  N7: RE4.EncoderPinA, Pico.pin_10
  N8: RE4.EncoderPinB, Pico.pin_9
  re4sw: RE4.SwitchPinE, Pico.pin_25
  N9: RE5.EncoderPinA, Pico.pin_7
  N10: RE5.EncoderPinB, Pico.pin_6
  re5sw: RE5.SwitchPinE, Pico.pin_26
  N11: RE6.EncoderPinA, Pico.pin_5
  N12: RE6.EncoderPinB, Pico.pin_4
  re6sw: RE6.SwitchPinE, Pico.pin_27
  N13: RE7.EncoderPinA, Pico.pin_2
  N14: RE7.EncoderPinB, Pico.pin_1
  re7sw: RE7.SwitchPinE, Pico.pin_29
  N15: RE8.EncoderPinA, Pico.pin_34
  N16: RE8.EncoderPinB, Pico.pin_32
  re8sw: RE8.SwitchPinE, Pico.pin_31

custom parts:
  Rotary Encoder: Rotary Encoder from ALPSec11e with switch.
  Raspberry Pi Pico: Raspberry Pi Pico. Based around the RP2040 microcontroller the Pico is a low cost microcontroller device bringing Raspberry Pi quality, cost, and easy of use to the microcontroller space. Jan 2021, Split part in to two versions: tht (this one) and SMD. This one will drill holes for a .1 in header in pcb to allow plugging in the module as well as providing pads to solder the module to the top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
